// Logisim project disp.circ as structural Verilog: 1 circuit, main circuit main
module main (
  output [15:0] r0,
  output [15:0] r1,
  output [15:0] r2,
  output [15:0] r3,
  output [15:0] d0,
  output [15:0] d1,
  output [15:0] Data_Mem_Data,
  output [15:0] Data_Mem_Addr,
  output Write_Enabled,
  output [15:0] Clock_Count,
  output halt
);

  wire main_1_p5;
  wire [15:0] adder_1_out, main_1_p9, main_1_p10, main_1_p11, rom_1_data;

  // Probe on main_1_p9
  // Probe on rom_1_data
  ROM #(.addrWidth(16), .dataWidth(16)) rom_1 (.addr(main_1_p9), .data(rom_1_data));  // open: sel
  // cpu_main main_1: pin names not known; wires that end beside it: rom_1_data, r0, r1, r2, main_1_p5, r3, d0, d1, main_1_p9, main_1_p10, main_1_p11, Write_Enabled
  Multiplexer #(.width(16), .enable("false")) multiplexer_1 (
    .in0({16{1'b0}}), .in1(main_1_p10), .out(Data_Mem_Data), .sel(Write_Enabled));
  Multiplexer #(.width(16), .enable("false")) multiplexer_2 (
    .in0({16{1'b0}}), .in1(main_1_p11), .out(Data_Mem_Addr), .sel(Write_Enabled));
  Clock clock_1 (.out(main_1_p5));
  Register #(.width(16)) register_1 (.D(adder_1_out), .Q(Clock_Count), .clk(main_1_p5));  // open: en, clr
  Adder #(.width(16)) adder_1 (.a(16'h1), .b(Clock_Count), .out(adder_1_out));  // open: cin, cout
  Comparator #(.width(16)) comparator_1 (.a(Clock_Count), .b(16'h10), .eq(halt));  // open: gt, lt

  // Notes on the sheet:
  //   Instruction Memory
  //   contents of rom_1 (hex, n*v repeats v):
  //   b1de 85ad c400 b2be 86ef c801 b0ca 80fe c000 b3ba 8fbe cc01
endmodule
